// Logisim project STE.circ as structural Verilog
module Display_7_segmentos (
  input  in_1,
  input  in_2,
  input  in_3,
  output out_4
);

  wire and_1_out, and_2_out, and_3_out, and_4_out, buffer_1_out, not_1_out, or_1_out, or_2_out, undriven,
       undriven_2, undriven_3, undriven_4;

  // NOT_Gate not_1 has open pins: in=open, out=not_1_out
  // Buffer buffer_1 has open pins: in=open, out=buffer_1_out
  and and_1 (and_1_out, not_1_out, undriven);
  and and_2 (and_2_out, undriven_2, buffer_1_out);
  and and_3 (and_3_out, undriven_3, undriven_4);
  and and_4 (and_4_out, in_1, in_2);
  or or_1 (or_1_out, and_1_out, and_2_out);
  nand nand_1 (out_4, and_4_out, in_3);
  or or_2 (or_2_out, or_1_out, and_3_out);
endmodule
