// Logisim project TTL_7segmentos.circ as structural Verilog: 1 circuit, main circuit main
module main (
);

  wire dipswitch_1_p3, dipswitch_1_p6, n7404_1_pin2, n7404_1_pin4, n7404_1_pin6, n7408_1_pin1, n7408_1_pin2,
       n7408_1_pin3, n7408_1_pin11, n7408_1_pin13, n7408_2_pin3, n7408_2_pin6, n7408_2_pin8, n7408_2_pin11,
       n7408_3_pin3, n7408_3_pin6, n7408_3_pin8, n7408_3_pin11, n7432_1_pin3, n7432_1_pin6, n7432_1_pin8,
       n7432_1_pin11, n7432_2_pin3, n7432_2_pin6, n7432_2_pin8, n7432_2_pin11, n7432_3_pin3, n7432_3_pin6,
       n7432_3_pin8, n7432_4_pin3;

  _7408 u_7408_1 (
    .pin1(n7408_1_pin1), .pin2(n7408_1_pin2), .pin3(n7408_1_pin3), .pin13(n7408_1_pin13),
    .pin12(n7408_1_pin2), .pin11(n7408_1_pin11));  // open: pin4, pin5, pin6, pin10, pin9, pin8
  // DipSwitch dipswitch_1: pin names not known; wires that end beside it: 1'b1, n7408_1_pin2, dipswitch_1_p3, n7408_1_pin1, n7408_1_pin13, dipswitch_1_p6, 1'b0, 1'b0
  _7404 u_7404_1 (
    .pin1(dipswitch_1_p3), .pin2(n7404_1_pin2), .pin3(n7408_1_pin1), .pin4(n7404_1_pin4),
    .pin5(n7408_1_pin13), .pin6(n7404_1_pin6), .pin13(dipswitch_1_p6), .pin12(n7408_1_pin2));  // open: pin11, pin10, pin9, pin8
  _7408 u_7408_2 (
    .pin1(n7408_1_pin1), .pin2(n7408_1_pin13), .pin3(n7408_2_pin3), .pin4(n7404_1_pin6),
    .pin5(dipswitch_1_p6), .pin6(n7408_2_pin6), .pin13(n7404_1_pin2), .pin12(n7404_1_pin4),
    .pin11(n7408_2_pin11), .pin10(n7408_2_pin11), .pin9(n7408_1_pin2), .pin8(n7408_2_pin8));
  _7408 u_7408_3 (
    .pin1(n7408_1_pin13), .pin2(dipswitch_1_p6), .pin3(n7408_3_pin3), .pin4(n7404_1_pin6),
    .pin5(dipswitch_1_p6), .pin6(n7408_3_pin6), .pin13(n7404_1_pin4), .pin12(n7404_1_pin6),
    .pin11(n7408_3_pin11), .pin10(n7408_2_pin3), .pin9(n7408_1_pin2), .pin8(n7408_3_pin8));
  _7432 u_7432_1 (
    .pin1(n7408_2_pin3), .pin2(n7408_2_pin6), .pin3(n7432_1_pin3), .pin4(n7432_1_pin3), .pin5(n7408_2_pin8),
    .pin6(n7432_1_pin6), .pin13(n7404_1_pin4), .pin12(n7408_3_pin3), .pin11(n7432_1_pin11),
    .pin10(n7404_1_pin4), .pin9(n7408_2_pin6), .pin8(n7432_1_pin8));
  _7432 u_7432_2 (
    .pin1(n7408_3_pin11), .pin2(n7408_3_pin6), .pin3(n7432_2_pin3), .pin4(n7432_2_pin3), .pin5(n7408_3_pin8),
    .pin6(n7432_2_pin6), .pin13(n7408_1_pin1), .pin12(dipswitch_1_p3), .pin11(n7432_2_pin11),
    .pin10(n7432_2_pin11), .pin9(n7408_3_pin6), .pin8(n7432_2_pin8));
  _7432 u_7432_3 (
    .pin1(n7432_2_pin8), .pin2(n7408_1_pin11), .pin3(n7432_3_pin3), .pin4(dipswitch_1_p3),
    .pin5(n7408_1_pin11), .pin6(n7432_3_pin6), .pin10(n7408_1_pin3), .pin9(n7408_2_pin3), .pin8(n7432_3_pin8));  // open: pin13, pin12, pin11
  _7432 u_7432_4 (
    .pin1(n7432_3_pin6), .pin2(n7432_3_pin8), .pin3(n7432_4_pin3));  // open: pin4, pin5, pin6, pin13, pin12, pin11, pin10, pin9, pin8
  _7_Segment_Display u_7_segment_display_1 (
    .g(n7432_1_pin6), .f(n7432_1_pin11), .a(n7432_2_pin6), .b(n7432_3_pin3), .e(n7432_1_pin8),
    .c(n7432_4_pin3));  // open: d, dp

  // Notes on the sheet:
  //   BD'
  //   A
  //   B
  //   C
  //   D
  //   A+CD"
  //   A+CD'+BD'+BC
  //   A'
  //   B'
  //   C'
  //   BC
  //   C'D
  //   C'D
  //   G
  //   B+A+C'D
  //   CD'
  //   D'
  //   C'
  //   F
  //   B+A+C'D+CD'
  //   B'
  //   B'C'
  //   A'B'D'
  //   B'
  //   B+A
  //   B'C'+C'D+BCD'
  //   '
  //   C'D
endmodule
