// Logisim project sete_segmentos.circ as structural Verilog: 1 circuit, main circuit main
module main (
  input  [7:0] E_F_D_DP_B_A_F_C
);

  _7_Segment_Display u_7_segment_display_1 (
    .g(E_F_D_DP_B_A_F_C[0]), .f(E_F_D_DP_B_A_F_C[1]), .a(E_F_D_DP_B_A_F_C[2]), .b(E_F_D_DP_B_A_F_C[3]),
    .e(E_F_D_DP_B_A_F_C[7]), .d(E_F_D_DP_B_A_F_C[6]), .c(E_F_D_DP_B_A_F_C[5]), .dp(E_F_D_DP_B_A_F_C[4]));
endmodule
